# Fritzing sketch RobotCar_nodeMCU (saved by Fritzing 0.9.3b)
breadboards: 1

parts:
  S3 = H-Bridge with L298N
  U1 = NodeMCU V1.0
  M2 = DC Motor
  M3 = DC Motor
  VCC1 = 4 x AAA Battery Mount

nets:
  12V: S3.12V, U1.Vin, VCC1.+
  GND: S3.GND, U1.GND, VCC1.-
  N1: S3.ENA, S3.ENA-5V
  N2: S3.IN1, U1.D0
  N3: S3.IN2, U1.D1
  N4: S3.IN3, U1.D3
  N5: S3.IN4, U1.D4
  N6: S3.M1-01, M3.pin_2
  N7: S3.M1-02, M3.pin_1
  N8: S3.M2-01, M2.pin_2
  N9: S3.M2-02, M2.pin_1

custom parts:
  H-Bridge with L298N: h-bridge
  NodeMCU V1.0: ESP8266 based NodeMCU
